# Fritzing sketch Circuit1 (saved by Fritzing 0.9.4)
breadboards: 1

parts:
  R1 = Resistor [tolerance=±5% resistance=220 package=THT]
  Part1 = Variable Capacitor [capacitance=100nF max_capacitance=10pF min_capacitance=2pF voltage=35V]
  Part2 = Arduino Uno (Rev3)

nets:
  N1: R1.Pin_0, Part2.D4
  N2: R1.Pin_1, Part1.0, Part2.D2
