# Fritzing sketch Circuit2-phase2 (saved by Fritzing 0.9.4)
breadboards: 1

parts:
  R1 = Resistor [tolerance=±5% resistance=1M package=THT]
  Part1 = Arduino Uno (Rev3)
  Part2 = Variable Capacitor [capacitance=100nF max_capacitance=10pF min_capacitance=2pF voltage=35V]
  LED1 = LED - 5mm [color="Red (633nm)" package="5 mm [THT]"]
  R2 = Resistor [tolerance=±5% resistance=220 package=THT]
  R3 = Resistor [tolerance=±5% resistance=1M package=THT]
  C1 = Capacitor [package=cap-pth-small2]

nets:
  N1: R1.Pin_0, Part1.D4
  N2: R1.Pin_1, Part2.2
  N3: Part1.GND, LED1.cathode, C1.2
  N4: Part1.D2, R3.Pin_1, C1.1
  N5: Part1.D5_PWM, R2.Pin_1
  N6: Part2.1, R3.Pin_0
  N7: LED1.anode, R2.Pin_0
