# Fritzing sketch Circuit3 (saved by Fritzing 0.9.4)
breadboards: 1

parts:
  U2 = 555 Timer [package="DIP8 [THT]"]
  R2 = Resistor [tolerance=±5% resistance=220 package="0402 [SMD]"]
  C3 = Capacitor [package=cap-pth-small2]
  R8 = Resistor [tolerance=±5% resistance=220 package="0402 [SMD]"]
  C4 = Capacitor [package=cap-pth-small2]
  LED1 = LED - 3mm [color="Red (633nm)" package="3 mm [THT]"]
  Part2 = Variable Capacitor [capacitance=100nF max_capacitance=10pF min_capacitance=2pF voltage=35V]
  U4 = 4011 4 x 2 Input NAND Gate, multi-part [part_number=4011 package="DIP (Dual Inline) [THT]"]
  part = 4011_4_x_2_input_NAND_gate_multipart_subpart1 [part_number=4011]  # not connected
  U4_1 = 4011_4_x_2_input_NAND_gate_multipart_subpart2 [part_number=4011]  # not connected
  U4_2 = 4011_4_x_2_input_NAND_gate_multipart_subpart3 [part_number=4011]  # not connected
  R9 = Trimmer Potentiometer [maximum_resistance=1MΩ package=THT]
  VCC2 = Battery block 9V
  R10 = Resistor [tolerance=±5% resistance=220 package="0402 [SMD]"]

nets:
  N1: U2.Ground, U2.Trigger, U2.Control_Voltage, U2.Threshold, R2.Pin_1, C3.1, C3.2, C4.1, C4.2, LED1.cathode, Part2.1, U4.connector0, U4.connector6, R9.leg1, R9.wiper, VCC2.-
  N2: U2.Output, Part2.2
  N3: U2.Reset, U2.Vcc_Supply_Voltage, R8.Pin_0, U4.connector1, U4.connector5, U4.connector13, VCC2.+
  N4: U2.Discharge, R2.Pin_0, R8.Pin_1
  N5: LED1.anode, R10.Pin_1
  N6: U4.connector2, U4.connector4
  N7: U4.connector3, R10.Pin_0
